// Logisim project MATERIAL EXTRA - EXPRESSÃO - PROJ. DE ENSINO.circ as structural Verilog: 1 circuit, main circuit main
module main (
  input  B,
  input  A,
  input  C,
  output S
);

  wire and_1_out, not_1_out, or_1_out, or_2_out;

  or or_1 (or_1_out, B, A);
  or or_2 (or_2_out, A, C);
  not not_1 (not_1_out, or_1_out);
  not not_2 (S, and_1_out);
  and and_1 (and_1_out, not_1_out, or_2_out);
endmodule
