// Logisim project MATERIAL EXTRA - PRENSA - PROJ. DE ENSINO.circ as structural Verilog: 1 circuit, main circuit main
module main (
  input  Alavanca_A,
  input  Alavanca_B,
  output Prensa
);

  wire and_1_out, button_1_out;

  Button button_1 (.out(button_1_out));
  and and_1 (and_1_out, Alavanca_A, Alavanca_B);
  or or_1 (Prensa, and_1_out, button_1_out);

  // Notes on the sheet:
  //   Botão C
endmodule
